# Fritzing sketch Thermal Printer (saved by Fritzing 0.9.3b)

parts:
  Part1 = Arduino Uno (Rev3)
  JACK1 = 2.1mm Barrel Jack with Terminal Block
  J1 = male pin header, 5 pins [form="♂ (male)"]
  J2 = male pin header, 2 pins [form="♂ (male)"]

nets:
  N1: Part1.GND, J1.pin5
  N2: Part1.D2, J1.pin2
  N3: Part1.D3_PWM, J1.pin3
  N4: JACK1.POS, J2.pin2
  N5: JACK1.NEG, J2.pin1

notes:
  GOOJPRT 58mm Receipt Thermal Printer
  (~£16, e.g. https://bit.ly/2kMHtf7)
  Legend on underside of printer states:
  NC (Black) - Not Connected
  TX (Blue) - Arduino Pin 2
  RX (Green) - Arduino Pin 3
  DTR (Yellow) - Not Connected
  GND (Red) - Arduino GND
  Note that the included cable harness was wired with *red* as the GND wire - very unusual!
  5V DC
